// Logisim project CO Final Project.circ as structural Verilog: 5 circuits, main circuit main
module main (
  input  CLR_AR,
  input  CLR_PC,
  input  INC_AC,
  input  CLR_AC,
  input  CLR_DR,
  input  LD_TR,
  input  INC_TR,
  input  CLR_TR,
  input  [15:0] in_9
);

  wire AC_Load, and_1_out, and_2_out, and_3_out, and_4_out, and_5_out, and_6_out, and_7_out, and_9_out,
       and_10_out, and_11_out, and_12_out, and_13_out, and_14_out, and_15_out, and_16_out, and_17_out,
       and_18_out, and_19_out, and_20_out, and_21_out, and_23_out, and_24_out, and_25_out, and_26_out,
       and_27_out, and_28_out, and_29_out, and_31_out, and_32_out, and_33_out, and_34_out, and_35_out,
       AR_INC, CLOCK_out, comparator_1_eq, D0, D1, D2, D3, D4, D5, D6, D7, d_ff_1_q, DR_INC, DR_Load,
       or_1_out, or_2_out, PC_INC, PC_Load, Read, T0, T1, T2, T3, T4, T5, T6, T7, T8, T9, T10, T11, T12, T13,
       T14, Write;
  wire [2:0] priority_encoder_1_out;
  wire [3:0] ALU_select, ALU_select_t, SC_q;
  wire [6:0] Address, AR_q, bit_extender_1_out, bit_extender_2_out, multiplexer_1_out, PC_q;
  wire [15:0] AC_q, ALU_output, bit_extender_3_out, bit_extender_4_out, DR_check, multiplexer_2_out,
       ram_1_data, TR_q;
  wire [15:7] IR_q;

  Clock CLOCK (.out(CLOCK_out));
  Bit_Extender #(.in_width(16), .out_width(7)) bit_extender_1 (.in(multiplexer_2_out), .out(bit_extender_1_out));
  and and_1 (and_1_out, D0, T4);
  and and_2 (and_2_out, D1, T4);
  and and_3 (and_3_out, D2, T4);
  and and_4 (and_4_out, D5, T4);
  and and_5 (and_5_out, D3, T3);
  and and_6 (and_6_out, D4, T3);
  and and_7 (and_7_out, D6, T6);
  Multiplexer #(.width(7), .enable("false")) multiplexer_1 (
    .in0(bit_extender_1_out), .in1(Address), .out(multiplexer_1_out), .sel(T2));
  Bit_Extender #(.in_width(16), .out_width(7)) bit_extender_2 (.in(multiplexer_2_out), .out(bit_extender_2_out));
  ALU ALU (.DR(DR_check), .AC(AC_q), .BUS(multiplexer_2_out), .C3C2C1C0(ALU_select_t), .OUTPUT(ALU_output));
  or or_1 (or_1_out, T0, T2);
  Counter #(.width(7), .max('h7f)) AR (
    .load(or_1_out), .D(multiplexer_1_out), .count(AR_INC), .Q(AR_q), .clk(CLOCK_out), .clr(CLR_AR));  // open: carry
  Counter #(.width(7), .max('h7f)) PC (
    .load(PC_Load), .D(bit_extender_2_out), .count(PC_INC), .Q(PC_q), .clk(CLOCK_out), .clr(CLR_PC));  // open: carry
  Counter #(.width(16), .max('hffff)) DR (
    .load(DR_Load), .D(multiplexer_2_out), .count(DR_INC), .Q(DR_check), .clk(CLOCK_out), .clr(CLR_DR));  // open: carry
  Counter #(.width(16), .max('hffff)) TR (
    .load(LD_TR), .D(multiplexer_2_out), .count(INC_TR), .Q(TR_q), .clk(CLOCK_out), .clr(CLR_TR));  // open: carry
  Register #(.width(16)) IR (.D(multiplexer_2_out), .en(T1), .Q({IR_q, Address}), .clk(CLOCK_out));  // open: clr
  D_Flip_Flop d_ff_1 (.clk(CLOCK_out), .D(or_2_out), .Q(d_ff_1_q));  // open: Qn, preset, en, reset
  Counter #(.width(4), .max('hf)) SC (.Q(SC_q), .clk(CLOCK_out), .clr(d_ff_1_q));  // open: load, D, count, carry
  assign bit_extender_3_out = {{9{1'b0}}, AR_q};  // Bit_Extender bit_extender_3
  assign bit_extender_4_out = {{9{1'b0}}, PC_q};  // Bit_Extender bit_extender_4
  Counter #(.width(16), .max('hffff)) AC (
    .load(AC_Load), .D(ALU_output), .count(INC_AC), .Q(AC_q), .clk(CLOCK_out), .clr(CLR_AC));  // open: carry
  or or_2 (or_2_out, and_1_out, and_2_out, and_3_out, and_4_out, and_5_out, and_6_out, and_7_out);
  Comparator #(.width(16)) comparator_1 (.a(DR_check), .b(in_9), .eq(comparator_1_eq));  // open: gt, lt
  RAM #(.addrWidth(7), .dataWidth(16), .bus("separate")) ram_1 (
    .addr(AR_q), .din(multiplexer_2_out), .data(ram_1_data), .str(Write), .clk(CLOCK_out), .ld(Read));  // open: sel, clr
  Decoder #(.select(3), .enable("false")) decoder_1 (
    .out0(D0), .out1(D1), .out2(D2), .out3(D3), .out4(D4), .out5(D5), .out6(D6), .out7(D7), .sel(IR_q[14:12]));
  Decoder #(.select(4), .enable("false")) decoder_2 (
    .out0(T0), .out1(T1), .out2(T2), .out3(T3), .out4(T4), .out5(T5), .out6(T6), .out7(T7), .out8(T8),
    .out9(T9), .out10(T10), .out11(T11), .out12(T12), .out13(T13), .out14(T14), .out15(T14), .sel(SC_q));
  and and_8 (DR_INC, D6, T4);
  and and_9 (and_9_out, comparator_1_eq, D6, T6);
  or or_3 (PC_INC, and_9_out, T1);
  Multiplexer #(.select(3), .width(16), .enable("false")) multiplexer_2 (
    .in1(bit_extender_3_out), .in2(bit_extender_4_out), .in3(AC_q), .in4(DR_check), .in5(TR_q),
    .in6(ram_1_data), .in7({IR_q, Address}), .out(multiplexer_2_out), .sel(priority_encoder_1_out));  // open: in0
  and and_10 (and_10_out, D4, T3);
  and and_11 (and_11_out, D3, T3);
  and and_12 (and_12_out, D6, T5);
  and and_13 (and_13_out, D0, T4);
  and and_14 (and_14_out, D1, T4);
  and and_15 (and_15_out, D2, T4);
  and and_16 (and_16_out, D5, T4);
  and and_17 (and_17_out, D0, T3);
  and and_18 (and_18_out, D1, T3);
  and and_19 (and_19_out, D2, T3);
  and and_20 (and_20_out, D5, T3);
  and and_21 (and_21_out, D6, T3);
  and and_22 (PC_Load, D4, T3);
  and and_23 (and_23_out, D3, T3);
  and and_24 (and_24_out, D6, T5);
  and and_25 (and_25_out, D0, T3);
  and and_26 (and_26_out, D1, T3);
  and and_27 (and_27_out, D2, T3);
  and and_28 (and_28_out, D5, T3);
  and and_29 (and_29_out, D6, T3);
  and and_30 (AR_INC, D5, T4);
  Priority_Encoder priority_encoder_1 (
    .in1(and_10_out), .in2(T0), .in3(and_11_out), .in4(and_12_out), .in6(Read), .out(priority_encoder_1_out));  // open: in0, in5, in7, en_in, gs, en_out
  and and_31 (and_31_out, D2, T4);
  and and_32 (and_32_out, D1, T4);
  and and_33 (and_33_out, D0, T4);
  and and_34 (and_34_out, D6, T4);
  or or_4 (AC_Load, and_13_out, and_14_out, and_15_out, and_16_out);
  or or_5 (DR_Load, and_17_out, and_18_out, and_19_out, and_20_out, and_21_out);
  or or_6 (Write, and_23_out, and_24_out);
  or or_7 (Read, and_25_out, and_26_out, and_27_out, and_28_out, and_29_out, T1);
  Priority_Encoder #(.select(4)) priority_encoder_2 (
    .in1(and_31_out), .in3(and_32_out), .in4(and_34_out), .in5(and_33_out), .in8(and_35_out), .out(ALU_select));  // open: in0, in2, in6, in7, in9, in10, in11, in12, in13, in14, in15, gs, en_out, en_in
  and and_35 (and_35_out, T4, D5);

  // Other names for the same wires on the sheet: T15 = T14
endmodule

module ALU (
  input  [15:0] DR,
  input  [15:0] AC,
  input  [15:0] BUS,
  input  [3:0] C3C2C1C0,
  output [15:0] OUTPUT
);

  wire [15:0] adder_1_out, adder_2_out, and_1_out, multiplier_1_out, multiplier_2_out, not_1_out, not_2_out;

  Adder #(.width(16)) adder_1 (.a(DR), .b(AC), .out(adder_1_out));  // open: cin, cout
  Adder #(.width(16)) adder_2 (.a(AC), .b(BUS), .out(adder_2_out));  // open: cin, cout
  assign not_1_out = ~AC;  // NOT_Gate not_1, 16 bits wide
  assign not_2_out = ~BUS;  // NOT_Gate not_2, 16 bits wide
  assign and_1_out = DR & AC;  // AND_Gate and_1, 16 bits wide
  Multiplier #(.width(16)) multiplier_1 (.a(DR), .b(AC), .out(multiplier_1_out));  // open: cin, cout
  Multiplier #(.width(16)) multiplier_2 (.a(AC), .b(BUS), .out(multiplier_2_out));  // open: cin, cout
  Multiplexer #(.select(4), .width(16)) multiplexer_1 (
    .in1(DR), .in2(BUS), .in3(adder_1_out), .in4(adder_2_out), .in5(and_1_out), .in6(not_1_out),
    .in7(not_2_out), .in8(multiplier_1_out), .in9(multiplier_2_out), .out(OUTPUT), .sel(C3C2C1C0));  // open: in0, in10, in11, in12, in13, in14, in15, en
endmodule

module ALU_CU (
  output [3:0] out_1
);

  wire and_1_out, and_2_out, and_3_out, and_4_out, D0, D1, D5, D6, T4;

  and and_1 (and_1_out, D1, T4);
  and and_2 (and_2_out, D0, T4);
  and and_3 (and_3_out, D6, T4);
  Priority_Encoder #(.select(4)) priority_encoder_1 (
    .in3(and_1_out), .in4(and_3_out), .in5(and_2_out), .in8(and_4_out), .out(out_1));  // open: in0, in1, in2, in6, in7, in9, in10, in11, in12, in13, in14, in15, gs, en_out, en_in
  and and_4 (and_4_out, T4, D5);
endmodule

module Bus_CU (
  output [2:0] out_1
);

  wire and_1_out, and_2_out, and_3_out, D3, D4, D6, Read, T3, T5;

  and and_1 (and_1_out, D4, T3);
  and and_2 (and_2_out, D3, T3);
  and and_3 (and_3_out, D6, T5);
  Priority_Encoder priority_encoder_1 (
    .in1(and_1_out), .in3(and_2_out), .in4(and_3_out), .in6(Read), .out(out_1));  // open: in0, in2, in5, in7, en_in, gs, en_out
endmodule

module SC_clear (
  output out_1
);

  wire and_1_out, and_2_out, and_3_out, and_4_out, and_5_out, and_6_out, and_7_out, D0, D1, D2, D3, D4, D5,
       D6, T3, T4, T6;

  and and_1 (and_1_out, D0, T4);
  and and_2 (and_2_out, D1, T4);
  and and_3 (and_3_out, D2, T4);
  and and_4 (and_4_out, D5, T4);
  and and_5 (and_5_out, D3, T3);
  and and_6 (and_6_out, D4, T3);
  and and_7 (and_7_out, D6, T6);
  or or_1 (out_1, and_1_out, and_2_out, and_3_out, and_4_out, and_5_out, and_6_out, and_7_out);
endmodule
